# Fritzing sketch esquema (saved by Fritzing 0.8.3b)
breadboards: 1

parts:
  Parte1 = Arduino Uno (Rev3)
  S1 = Pushbutton [package="[THT]"]
  R1 = Resistor [tolerance=±5% resistance=330 package=THT]
  LED1 = LED - 5mm [color="Red (633nm)" package="5 mm [THT]"]
  R2 = Resistor [tolerance=±5% resistance=330 package=THT]

nets:
  N1: Parte1.GND, Parte1.D2, S1.Pin_1, S1.Pin_2, S1.Pin_3, S1.Pin_4, R1.Pin_0, R2.Pin_1
  N2: Parte1.D12/MISO, LED1.anode
  N3: Parte1.5V, R1.Pin_1
  N4: LED1.cathode, R2.Pin_0
