# Fritzing sketch esquema (saved by Fritzing 0.8.3b)
breadboards: 1

parts:
  Parte1 = Arduino Uno (Rev3)
  S1 = Pushbutton [package="[THT]"]
  R1 = Resistor [tolerance=±5% resistance=330 package=THT]
  LED1 = LED - 5mm [color="Red (633nm)" package="5 mm [THT]"]
  R2 = Resistor [tolerance=±5% resistance=330 package=THT]
  LED2 = LED - 5mm [color="Yellow (595nm)" package="5 mm [THT]"]
  LED3 = LED - 5mm [color="Green (565nm)" package="5 mm [THT]"]
  R3 = Resistor [tolerance=±5% resistance=330 package=THT]
  R4 = Resistor [tolerance=±5% resistance=330 package=THT]
  LED4 = LED - 5mm [color="Green (565nm)" package="5 mm [THT]"]
  LED5 = LED - 5mm [color="Red (633nm)" package="5 mm [THT]"]

nets:
  N1: Parte1.GND, Parte1.D2, S1.Pin_1, S1.Pin_2, S1.Pin_3, S1.Pin_4, R1.Pin_0, R2.Pin_1, R3.Pin_1, R4.Pin_1
  N2: Parte1.D10_PWM/SS, LED3.anode
  N3: Parte1.D11_PWM/MOSI, LED2.anode
  N4: Parte1.D12/MISO, LED1.anode
  N5: Parte1.5V, R1.Pin_1
  N6: LED1.cathode, LED4.anode
  N7: R2.Pin_0, LED4.cathode
  N8: LED2.cathode, R3.Pin_0
  N9: LED3.cathode, LED5.anode
  N10: R4.Pin_0, LED5.cathode
