# Fritzing sketch esquema (saved by Fritzing 0.8.3b)

parts:
  PART1 = Motor Driver 1A Dual TB6612FNG [part_number=ROB_09457]
  shield1 = Iteaduino Bluetooth shield V2.1  # not connected
  M1 = DC Motor
  M2 = DC Motor
  VCC1 = 4 x AAA Battery Mount
  Parte1 = Arduino Leonardo (Rev3b)

nets:
  N1: PART1.PWMA, VCC1.+
  N2: PART1.AIN2, Parte1.5V
  N3: PART1.AIN1, VCC1.-, Parte1.GND
  N4: PART1.STBY, M2.pin_2
  N5: PART1.BIN1, M2.pin_1
  N6: PART1.BIN2, M1.pin_2
  N7: PART1.PWMB, M1.pin_1
  N8: PART1.VM, Parte1.D3_PWM/SCL
  N9: PART1.VCC, Parte1.D8/A8
  N10: PART1.GND, Parte1.D9_PWM/A9

custom parts:
  Motor Driver 1A Dual TB6612FNG: The TB6612FNG motor driver can control up to two DC motors at a constant current of 1.2A (3.2A peak). Two input signals (IN1 and IN2) can be used to control the motor in one of four function modes - CW, CCW, short-brake, and stop. The two motor outputs (A and B) can be separately controlled, the speed of each motor is controlled via a PWM input signal with a frequency up to 100kHz. The STBY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
  Iteaduino Bluetooth shield V2.1: The official support forum: support@iteadstudio.com
